# Fritzing sketch yarhzeit_adapter_shield (saved by Fritzing 0.9.2b)
circuit board: 5.4cm x 5.4cm
circuit board: 10.16cm x 5.36194cm
breadboards: 1

parts:
  YAHRZEIT_ADAPTER_SHIELD = Arduino Mega 2560 (Rev3)
  YYZ_PXL = shrouded pin header, 10 pins [form="♂ (shrouded male)"]

nets:
  N1: YAHRZEIT_ADAPTER_SHIELD.GND, YYZ_PXL.pin1, YYZ_PXL.pin10
  N2: YAHRZEIT_ADAPTER_SHIELD.D42, YYZ_PXL.pin5
  N3: YAHRZEIT_ADAPTER_SHIELD.D44, YYZ_PXL.pin4, YYZ_PXL.pin7
  N4: YAHRZEIT_ADAPTER_SHIELD.D46, YYZ_PXL.pin3, YYZ_PXL.pin8
  N5: YAHRZEIT_ADAPTER_SHIELD.D48, YYZ_PXL.pin2, YYZ_PXL.pin9
